# Fritzing sketch ServoHAT (saved by Fritzing 0.9.5d)

parts:
  Part1 = Adafruit DC+Stepper Motor HAT [part_number="Adafruit #2348"]
  M1 = Stepper Motor - Bipolar
  M2 = Stepper Motor - Bipolar

nets:
  N1: Part1.M2A, M1.A
  N2: Part1.M2B, M1.C
  N3: Part1.M1B, M1.B
  N4: Part1.M1A, M1.D
  N5: Part1.M4A, M2.A
  N6: Part1.M4B, M2.C
  N7: Part1.M3B, M2.B
  N8: Part1.M3A, M2.D

custom parts:
  Adafruit DC+Stepper Motor HAT: Let your robotic dreams come true with the new DC+Stepper Motor HAT from Adafruit. This Raspberry Pi add-on is perfect for any motion project as it can drive up to 4 DC or 2 Stepper motors with full PWM speed control. Since the Raspberry Pi does not have a lot of PWM pins, we use a fully-dedicated PWM driver chip onboard to both control motor direction and speed. This chip handles all the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
